# Fritzing sketch StreamCon V1_7 (saved by Fritzing 0.9.3b)
circuit board: 10cm x 10cm
breadboards: 1

parts:
  B11 = double row female pin header, 2 pins [form="♀ (female)"]
  B21 = double row female pin header, 2 pins [form="♀ (female)"]
  B31 = double row female pin header, 2 pins [form="♀ (female)"]
  B41 = double row female pin header, 2 pins [form="♀ (female)"]
  B12 = double row female pin header, 2 pins [form="♀ (female)"]
  B22 = double row female pin header, 2 pins [form="♀ (female)"]
  B32 = double row female pin header, 2 pins [form="♀ (female)"]
  B42 = double row female pin header, 2 pins [form="♀ (female)"]
  B13 = double row female pin header, 2 pins [form="♀ (female)"]
  B23 = double row female pin header, 2 pins [form="♀ (female)"]
  B33 = double row female pin header, 2 pins [form="♀ (female)"]
  B43 = double row female pin header, 2 pins [form="♀ (female)"]
  B24 = double row female pin header, 2 pins [form="♀ (female)"]
  B34 = double row female pin header, 2 pins [form="♀ (female)"]
  B44 = double row female pin header, 2 pins [form="♀ (female)"]
  L34 = double row female pin header, 2 pins [form="♀ (female)"]
  L24 = double row female pin header, 2 pins [form="♀ (female)"]
  L31 = double row female pin header, 2 pins [form="♀ (female)"]
  L22 = double row female pin header, 2 pins [form="♀ (female)"]
  L12 = double row female pin header, 2 pins [form="♀ (female)"]
  L21 = double row female pin header, 2 pins [form="♀ (female)"]
  L14 = double row female pin header, 2 pins [form="♀ (female)"]
  L13 = double row female pin header, 2 pins [form="♀ (female)"]
  L32 = double row female pin header, 2 pins [form="♀ (female)"]
  L42 = double row female pin header, 2 pins [form="♀ (female)"]
  L33 = double row female pin header, 2 pins [form="♀ (female)"]
  L43 = double row female pin header, 2 pins [form="♀ (female)"]
  L41 = double row female pin header, 2 pins [form="♀ (female)"]
  L23 = double row female pin header, 2 pins [form="♀ (female)"]
  L44 = double row female pin header, 2 pins [form="♀ (female)"]
  J33 = female pin header, 17 pins [form="♀ (female)"]
  J36 = female pin header, 17 pins [form="♀ (female)"]
  J41 = female pin header, 3 pins [form="♀ (female)"]
  J42 = female pin header, 3 pins [form="♀ (female)"]
  J43 = female pin header, 3 pins [form="♀ (female)"]
  J44 = female pin header, 3 pins [form="♀ (female)"]
  J45 = double row female pin header, 2 pins [form="♀ (female)"]
  J46 = double row female pin header, 2 pins [form="♀ (female)"]
  J47 = double row female pin header, 2 pins [form="♀ (female)"]
  J48 = double row female pin header, 2 pins [form="♀ (female)"]
  R1 = Resistor [tolerance=±5% resistance=1k package=THT]
  R2 = Resistor [tolerance=±5% resistance=1k package=THT]
  R4 = Resistor [tolerance=±5% resistance=1k package=THT]
  R5 = Resistor [tolerance=±5% resistance=1k package=THT]
  R6 = Resistor [tolerance=±5% resistance=1k package=THT]
  R7 = Resistor [tolerance=±5% resistance=1k package=THT]
  R8 = Resistor [tolerance=±5% resistance=1k package=THT]
  R9 = Resistor [tolerance=±5% resistance=1k package=THT]
  R10 = Resistor [tolerance=±5% resistance=1k package=THT]
  R11 = Resistor [tolerance=±5% resistance=1k package=THT]
  R3 = Resistor [tolerance=±5% resistance=1k package=THT]
  R0 = Resistor [tolerance=±5% resistance=1k package=THT]
  R12 = Resistor [tolerance=±5% resistance=1k package=THT]
  R13 = Resistor [tolerance=±5% resistance=1k package=THT]
  R14 = Resistor [tolerance=±5% resistance=1k package=THT]
  R15 = Resistor [tolerance=±5% resistance=1k package=THT]
  J49 = double row female pin header, 2 pins [form="♀ (female)"]
  L11 = double row female pin header, 2 pins [form="♀ (female)"]
  B14 = double row female pin header, 2 pins [form="♀ (female)"]
  J35 = female pin header, 15 pins [form="♀ (female)"]
  J34 = female pin header, 15 pins [form="♀ (female)"]
  J50 = female pin header, 4 pins [form="♀ (female)"]

nets:
  N1: B11.pin1, B21.pin1, B31.pin1, B41.pin1, B12.pin1, B22.pin1, B32.pin1, B42.pin1, B13.pin1, B23.pin1, B33.pin1, B43.pin1, B24.pin1, B34.pin1, B44.pin1, J33.pin2, J41.pin1, J42.pin1, J43.pin1, J44.pin1, J49.pin2, B14.pin1
  N2: B11.pin2, J33.pin6, R11.Pin_0
  N3: B21.pin2, J33.pin7, R10.Pin_0
  N4: B31.pin2, J33.pin8, R9.Pin_0
  N5: B41.pin2, J33.pin9, R8.Pin_0
  N6: B12.pin2, J33.pin10, R7.Pin_0
  N7: B22.pin2, J33.pin11, R6.Pin_0
  N8: B32.pin2, J33.pin12, R5.Pin_0
  N9: B42.pin2, J33.pin13, R4.Pin_0
  N10: B13.pin2, J33.pin14, R3.Pin_0
  N11: B23.pin2, J33.pin15, R2.Pin_0
  N12: B33.pin2, J33.pin16, R1.Pin_0
  N13: B43.pin2, J33.pin17, R0.Pin_0
  N14: B24.pin2, J33.pin4, R13.Pin_0
  N15: B34.pin2, R14.Pin_1, J34.pin4
  N16: B44.pin2, R15.Pin_1, J34.pin3
  N17: L34.pin1, L24.pin1, L31.pin1, L22.pin1, L12.pin1, L21.pin1, L14.pin1, L13.pin1, L32.pin1, L42.pin1, L33.pin1, L43.pin1, L41.pin1, L23.pin1, L44.pin1, L11.pin1, J35.pin2
  N18: L34.pin2, J36.pin12
  N19: L24.pin2, J36.pin11
  N20: L31.pin2, J35.pin13
  N21: L22.pin2, J35.pin4
  N22: L12.pin2, J35.pin3
  N23: L21.pin2, J35.pin12
  N24: L14.pin2, J36.pin10
  N25: L13.pin2, J36.pin6
  N26: L32.pin2, J35.pin5
  N27: L42.pin2, J35.pin6
  N28: L33.pin2, J36.pin8
  N29: L43.pin2, J36.pin9
  N30: L41.pin2, J35.pin14
  N31: L23.pin2, J36.pin7
  N32: L44.pin2, J36.pin13
  N33: J33.pin1, R1.Pin_1, R2.Pin_1, R4.Pin_1, R5.Pin_1, R6.Pin_1, R7.Pin_1, R8.Pin_1, R9.Pin_1, R10.Pin_1, R11.Pin_1, R3.Pin_1, R0.Pin_1, R12.Pin_1, R13.Pin_1
  N34: J33.pin5, R12.Pin_0, B14.pin2
  N35: J36.pin1, J41.pin2, J42.pin2, J43.pin2, J44.pin2, R14.Pin_0, R15.Pin_0, J34.pin2, J50.pin4
  N36: J36.pin2, J50.pin3
  N37: J36.pin4, J50.pin2
  N38: J36.pin5, J50.pin1
  N39: J36.pin14, J45.pin2
  N40: J36.pin15, J46.pin2
  N41: J36.pin16, J47.pin2
  N42: J36.pin17, J48.pin2
  N43: J41.pin3, J34.pin8
  N44: J42.pin3, J34.pin7
  N45: J43.pin3, J34.pin5
  N46: J44.pin3, J34.pin6
  N47: J45.pin1, J34.pin14
  N48: J46.pin1, J34.pin13
  N49: J47.pin1, J34.pin12
  N50: J48.pin1, J34.pin11
  N51: J49.pin1, J35.pin1
  N52: L11.pin2, J35.pin11

notes:
  5v
  GND
  13
  12
  11
  10
  9
  4
  8
  6
  7
  5
  1
  0
  3
  2
  A5
  A0
  A4
  A2
  A3
  A1
  TX
  3v3
  17
  16
  15
  14
  VIN
  MAIN CONTROL
  LIGHT CONTROL
  DIY Stream Controller V1.7.1
  Glitch1 2019
  RX
  -
  +
  s
  RST
  RGB
  DI
  DO
  github.com/GlitchOne
